// Logisim project lastname_firstname.circ as structural Verilog: 7 circuits, main circuit main
module main (
);

  wire B, Clock, EnOFF, Jump, Reg2Read, RegToWr;
  wire [1:0] Func, rom_2_data, rom_2_data_3;
  wire [2:0] Opcode;
  wire [3:0] multiplexer_2_out, RegToWr_In, Rx, Ry, Rz;
  wire [7:0] PC_q, PC_q_2, PC_q_3, PC_q_4;
  wire [8:5] rom_2_data_2;
  wire [19:0] controlled_buffer_1_out;
  wire [31:0] adder_1_out, bit_extender_1_out, dual_ported_register_file_1_out1,
       dual_ported_register_file_1_out2, idrr_ex_buffer_1_a_out, idrr_ex_buffer_1_b_out, multiplexer_1_out,
       multiplexer_4_out, PC, rom_1_data;
  wire [31:4] if_idrr_buffer_1_instruction_out;

  Register #(.width(32)) u_PC (
    .D(multiplexer_1_out), .en(1'b1), .Q({PC_q, PC_q_4, PC_q_3, PC_q_2}), .clk(Clock));  // open: clr
  Clock clock_1 (.out(Clock));
  Multiplexer #(.select(2), .width(32)) multiplexer_1 (
    .in0(adder_1_out), .out(multiplexer_1_out), .en(1'b1));  // open: in1, in2, in3, sel
  Adder #(.width(32)) adder_1 (.a({PC_q, PC_q_4, PC_q_3, PC_q_2}), .b(32'h1), .out(adder_1_out));  // open: cin, cout
  ROM #(.addrWidth(24), .dataWidth(32)) rom_1 (.addr({PC_q_4, PC_q_3, PC_q_2}), .data(rom_1_data));  // open: sel
  IF_IDRR_Buffer if_idrr_buffer_1 (
    .Instruction_In(rom_1_data), .PC_In(adder_1_out),
    .Instruction_Out({if_idrr_buffer_1_instruction_out[31], Opcode, Rx, Ry, if_idrr_buffer_1_instruction_out[19:4], Rz}),
    .PC_Out(PC), .Clock(Clock));
  assign controlled_buffer_1_out = EnOFF ? {if_idrr_buffer_1_instruction_out[19:4], Rz} : 20'bz;  // Controlled_Buffer controlled_buffer_1
  ROM #(.addrWidth(3), .dataWidth(11)) rom_2 (
    .addr(Opcode), .data({rom_2_data_3, rom_2_data_2, rom_2_data, RegToWr, B, Reg2Read}));  // open: sel
  Multiplexer #(.width(4)) multiplexer_2 (.in0(Rx), .in1(Rz), .out(multiplexer_2_out), .sel(Reg2Read), .en(1'b1));
  assign bit_extender_1_out = {{12{controlled_buffer_1_out[19]}}, controlled_buffer_1_out};  // Bit_Extender bit_extender_1
  Multiplexer #(.width(4)) multiplexer_3 (.in0(Rx), .in1(Ry), .out(RegToWr_In), .sel(RegToWr), .en(1'b1));
  Dual_Ported_Register_File dual_ported_register_file_1 (
    .CLK(Clock), .RdREGNO1(Ry), .RdREGNO2(multiplexer_2_out), .OUT1(dual_ported_register_file_1_out1),
    .OUT2(dual_ported_register_file_1_out2));  // open: WrREGNO, INPUT, WrEN
  Multiplexer #(.width(32)) multiplexer_4 (
    .in0(dual_ported_register_file_1_out2), .in1(bit_extender_1_out), .out(multiplexer_4_out), .sel(B),
    .en(1'b1));
  IDRR_EX_Buffer idrr_ex_buffer_1 (
    .LdMem_In(rom_2_data_2[6]), .WrMem_In(rom_2_data_2[7]), .WrReg_In(rom_2_data_2[8]),
    .DataToWr_In(rom_2_data_3), .RegToWr_In(RegToWr_In), .A_In(dual_ported_register_file_1_out1),
    .A_Out(idrr_ex_buffer_1_a_out), .Rx_Contents_In(dual_ported_register_file_1_out2), .PC_In(PC),
    .B_In(multiplexer_4_out), .B_Out(idrr_ex_buffer_1_b_out), .Jump_In(rom_2_data_2[5]), .Jump_Out(Jump),
    .Func_In(rom_2_data), .Func_Out(Func));  // open: Clock, LdMem_Out, WrMem_Out, WrReg_Out, DataToWr_Out, RegToWr_Out, Rx_Contents_Out, PC_Out
  ALU alu_1 (.FUNC(Func), .A(idrr_ex_buffer_1_a_out), .B(idrr_ex_buffer_1_b_out));  // open: OUT
  ALU alu_2 ();  // open: FUNC, A, B, OUT
endmodule

module Dual_Ported_Register_File (
  input  CLK,
  input  WrEN,
  input  [3:0] WrREGNO,
  input  [3:0] RdREGNO1,
  input  [3:0] RdREGNO2,
  input  [31:0] INPUT,
  output [31:0] OUT1,
  output [31:0] OUT2
);

  wire En_a0, En_a1, En_a2, En_a3, En_a4, En_at, En_fp, En_k0, En_ra, En_s0, En_s1, En_s2, En_s3, En_sp,
       En_v0;
  wire [31:0] a0, a1, a2, a3, a4, at, fp, k0, ra, s0, s1, s2, s3, sp, v0, zero;

  Decoder #(.select(4), .disabled(0)) decoder_1 (
    .out1(En_at), .out2(En_v0), .out3(En_a0), .out4(En_a1), .out5(En_a2), .out6(En_a3), .out7(En_a4),
    .out8(En_s0), .out9(En_s1), .out10(En_s2), .out11(En_s3), .out12(En_k0), .out13(En_sp), .out14(En_fp),
    .out15(En_ra), .sel(WrREGNO), .en(WrEN));  // open: out0
  Register #(.width(32)) u_zero (.D(INPUT), .en(1'b0), .Q(zero), .clk(CLK));  // open: clr
  Register #(.width(32)) u_at (.D(INPUT), .en(En_at), .Q(at), .clk(CLK));  // open: clr
  Register #(.width(32)) u_v0 (.D(INPUT), .en(En_v0), .Q(v0), .clk(CLK));  // open: clr
  Register #(.width(32)) u_a0 (.D(INPUT), .en(En_a0), .Q(a0), .clk(CLK));  // open: clr
  Register #(.width(32)) u_a1 (.D(INPUT), .en(En_a1), .Q(a1), .clk(CLK));  // open: clr
  Register #(.width(32)) u_a2 (.D(INPUT), .en(En_a2), .Q(a2), .clk(CLK));  // open: clr
  Register #(.width(32)) u_a3 (.D(INPUT), .en(En_a3), .Q(a3), .clk(CLK));  // open: clr
  Register #(.width(32)) u_a4 (.D(INPUT), .en(En_a4), .Q(a4), .clk(CLK));  // open: clr
  Multiplexer #(.select(4), .width(32), .disabled(0), .enable("false")) multiplexer_1 (
    .in0(zero), .in1(at), .in2(v0), .in3(a0), .in4(a1), .in5(a2), .in6(a3), .in7(a4), .in8(s0), .in9(s1),
    .in10(s2), .in11(s3), .in12(k0), .in13(sp), .in14(fp), .in15(ra), .out(OUT2), .sel(RdREGNO2));
  Register #(.width(32)) u_s0 (.D(INPUT), .en(En_s0), .Q(s0), .clk(CLK));  // open: clr
  Register #(.width(32)) u_s1 (.D(INPUT), .en(En_s1), .Q(s1), .clk(CLK));  // open: clr
  Register #(.width(32)) u_s2 (.D(INPUT), .en(En_s2), .Q(s2), .clk(CLK));  // open: clr
  Register #(.width(32)) u_s3 (.D(INPUT), .en(En_s3), .Q(s3), .clk(CLK));  // open: clr
  Register #(.width(32)) u_k0 (.D(INPUT), .en(En_k0), .Q(k0), .clk(CLK));  // open: clr
  Register #(.width(32)) u_sp (.D(INPUT), .en(En_sp), .Q(sp), .clk(CLK));  // open: clr
  Register #(.width(32)) u_fp (.D(INPUT), .en(En_fp), .Q(fp), .clk(CLK));  // open: clr
  Register #(.width(32)) u_ra (.D(INPUT), .en(En_ra), .Q(ra), .clk(CLK));  // open: clr
  Multiplexer #(.select(4), .width(32), .disabled(0), .enable("false")) multiplexer_2 (
    .in0(zero), .in1(at), .in2(v0), .in3(a0), .in4(a1), .in5(a2), .in6(a3), .in7(a4), .in8(s0), .in9(s1),
    .in10(s2), .in11(s3), .in12(k0), .in13(sp), .in14(fp), .in15(ra), .out(OUT1), .sel(RdREGNO1));

  // Notes on the sheet:
  //   MODIFY AT YOUR OWN RISK
endmodule

module IF_IDRR_Buffer (
  input  [31:0] Instruction_In,
  input  Clock,
  input  [31:0] PC_In,
  output [31:0] Instruction_Out,
  output [31:0] PC_Out
);

  Register #(.width(32)) register_1 (.D(Instruction_In), .en(1'b1), .Q(Instruction_Out), .clk(Clock));  // open: clr
  Register #(.width(32)) register_2 (.D(PC_In), .en(1'b1), .Q(PC_Out), .clk(Clock));  // open: clr
endmodule

module IDRR_EX_Buffer (
  input  Clock,
  input  [1:0] Func_In,
  input  Jump_In,
  input  LdMem_In,
  input  WrMem_In,
  input  WrReg_In,
  input  [1:0] DataToWr_In,
  input  [3:0] RegToWr_In,
  input  [31:0] A_In,
  input  [31:0] B_In,
  input  [31:0] Rx_Contents_In,
  input  [31:0] PC_In,
  output [1:0] Func_Out,
  output Jump_Out,
  output LdMem_Out,
  output WrMem_Out,
  output WrReg_Out,
  output [1:0] DataToWr_Out,
  output [3:0] RegToWr_Out,
  output [31:0] A_Out,
  output [31:0] B_Out,
  output [31:0] Rx_Contents_Out,
  output [31:0] PC_Out
);

  Register #(.width(2)) register_1 (.D(Func_In), .en(1'b1), .Q(Func_Out), .clk(Clock));  // open: clr
  Register #(.width(1)) register_2 (.D(Jump_In), .en(1'b1), .Q(Jump_Out), .clk(Clock));  // open: clr
  Register #(.width(1)) register_3 (.D(LdMem_In), .en(1'b1), .Q(LdMem_Out), .clk(Clock));  // open: clr
  Register #(.width(1)) register_4 (.D(WrMem_In), .en(1'b1), .Q(WrMem_Out), .clk(Clock));  // open: clr
  Register #(.width(1)) register_5 (.D(WrReg_In), .en(1'b1), .Q(WrReg_Out), .clk(Clock));  // open: clr
  Register #(.width(2)) register_6 (.D(DataToWr_In), .en(1'b1), .Q(DataToWr_Out), .clk(Clock));  // open: clr
  Register #(.width(4)) register_7 (.D(RegToWr_In), .en(1'b1), .Q(RegToWr_Out), .clk(Clock));  // open: clr
  Register #(.width(32)) register_8 (.D(A_In), .en(1'b1), .Q(A_Out), .clk(Clock));  // open: clr
  Register #(.width(32)) register_9 (.D(B_In), .en(1'b1), .Q(B_Out), .clk(Clock));  // open: clr
  Register #(.width(32)) register_10 (.D(Rx_Contents_In), .en(1'b1), .Q(Rx_Contents_Out), .clk(Clock));  // open: clr
  Register #(.width(32)) register_11 (.D(PC_In), .en(1'b1), .Q(PC_Out), .clk(Clock));  // open: clr
endmodule

module EX_MEM_Buffer (
  input  Clock,
  input  LdMem_In,
  input  WrMem_In,
  input  WrReg_In,
  input  [1:0] DataToWr_In,
  input  [3:0] RegToWr_In,
  input  [31:0] ALU_In,
  input  [31:0] DataToWrMem_In,
  input  [31:0] PC_In,
  output LdMem_Out,
  output WrMem_Out,
  output WrReg_Out,
  output [1:0] DataToWr_Out,
  output [3:0] RegToWr_Out,
  output [31:0] ALU_Out,
  output [31:0] DataToWrMem_Out,
  output [31:0] PC_Out
);

  Register #(.width(1)) register_1 (.D(LdMem_In), .en(1'b1), .Q(LdMem_Out), .clk(Clock));  // open: clr
  Register #(.width(1)) register_2 (.D(WrMem_In), .en(1'b1), .Q(WrMem_Out), .clk(Clock));  // open: clr
  Register #(.width(1)) register_3 (.D(WrReg_In), .en(1'b1), .Q(WrReg_Out), .clk(Clock));  // open: clr
  Register #(.width(2)) register_4 (.D(DataToWr_In), .en(1'b1), .Q(DataToWr_Out), .clk(Clock));  // open: clr
  Register #(.width(4)) register_5 (.D(RegToWr_In), .en(1'b1), .Q(RegToWr_Out), .clk(Clock));  // open: clr
  Register #(.width(32)) register_6 (.D(ALU_In), .en(1'b1), .Q(ALU_Out), .clk(Clock));  // open: clr
  Register #(.width(32)) register_7 (.D(DataToWrMem_In), .en(1'b1), .Q(DataToWrMem_Out), .clk(Clock));  // open: clr
  Register #(.width(32)) register_8 (.D(PC_In), .en(1'b1), .Q(PC_Out), .clk(Clock));  // open: clr
endmodule

module MEM_WB_Buffer (
  input  Clock,
  input  WrReg_In,
  input  [1:0] DataToWr_In,
  input  [3:0] RegToWr_In,
  input  [31:0] ALU_In,
  input  [31:0] D_MEM_In,
  output WrReg_Out,
  output [1:0] DataToWr_Out,
  output [3:0] RegToWr_Out,
  output [31:0] ALU_Out,
  output [31:0] D_MEM_Out
);

  Register #(.width(1)) register_1 (.D(WrReg_In), .en(1'b1), .Q(WrReg_Out), .clk(Clock));  // open: clr
  Register #(.width(2)) register_2 (.D(DataToWr_In), .en(1'b1), .Q(DataToWr_Out), .clk(Clock));  // open: clr
  Register #(.width(4)) register_3 (.D(RegToWr_In), .en(1'b1), .Q(RegToWr_Out), .clk(Clock));  // open: clr
  Register #(.width(32)) register_4 (.D(ALU_In), .en(1'b1), .Q(ALU_Out), .clk(Clock));  // open: clr
  Register #(.width(32)) register_5 (.D(D_MEM_In), .en(1'b1), .Q(D_MEM_Out), .clk(Clock));  // open: clr
endmodule

module ALU (
  input  [1:0] FUNC,
  input  [31:0] A,
  input  [31:0] B,
  output [31:0] OUT
);

  wire [31:0] adder_1_out, adder_2_out, nand_1_out, subtractor_1_out;

  Adder #(.width(32)) adder_1 (.a(A), .b(B), .out(adder_1_out), .cin(1'b0));  // open: cout
  assign nand_1_out = ~(A & B);  // NAND_Gate nand_1, 32 bits wide
  Subtractor #(.width(32)) subtractor_1 (.a(A), .b(B), .out(subtractor_1_out), .bin(1'b0));  // open: bout
  Adder #(.width(32)) adder_2 (.a(A), .b({32{1'b0}}), .out(adder_2_out), .cin(1'b1));  // open: cout
  Multiplexer #(.select(2), .width(32), .disabled(0), .enable("false")) multiplexer_1 (
    .in0(adder_1_out), .in1(nand_1_out), .in2(subtractor_1_out), .in3(adder_2_out), .out(OUT), .sel(FUNC));

  // Notes on the sheet:
  //   MODIFY AT YOUR OWN RISK
endmodule
